# Fritzing sketch Design (saved by Fritzing 0.9.3b)
breadboards: 2

parts:
  U1 = NodeMCU V1.0
  GY1 = GY-5150 (MPU-9150) [form="♀ (female)" package=THT]
  Squix1 = OLED 0.96" 128x64 I2C SSD1306
  SEN1 = Pulse Sensor [package=SIP-3]
  BAT1 = Battery Holders [package=battcon_12mm]
  M1 = DC Motor
  U2 = TRANSISTOR_NPN_2 [package=to-92]

nets:
  N1: U1.D1, GY1.pin3, Squix1.SCL
  N2: U1.D2, GY1.pin4, Squix1.SCA
  N3: U1.D3, SEN1.Signal
  N4: U1.D4, U2.B
  VCC: U1.3V3, GY1.pin1, Squix1.VCC, SEN1.VCC, BAT1.-, M1.pin_1
  GND: U1.GND, GY1.pin2, Squix1.GND, SEN1.GND, BAT1.+, U2.C
  N5: M1.pin_2, U2.E

custom parts:
  NodeMCU V1.0: ESP8266 based NodeMCU
  GY-5150 (MPU-9150): Placa GY-5150 basada en conjunto de acelerómetro+giroscopios+magnetómetro MPU-9150
  Pulse Sensor: Pulse Sensor Optical Heart Beat Sensor
