# Fritzing sketch Sketch (saved by Fritzing 0.9.3b)
breadboards: 2

parts:
  U1 = NodeMCU V1.0
  GY1 = GY-5150 (MPU-9150) [form="♀ (female)" package=THT]  # not connected
  Squix1 = OLED 0.96" 128x64 I2C SSD1306

nets:
  N1: U1.D1, Squix1.SCL
  N2: U1.D2, Squix1.SCA
  3V3: U1.3V3, Squix1.VCC
  GND: U1.GND, Squix1.GND

custom parts:
  NodeMCU V1.0: ESP8266 based NodeMCU
  GY-5150 (MPU-9150): Placa GY-5150 basada en conjunto de acelerómetro+giroscopios+magnetómetro MPU-9150
